// Logisim project 5.circ as structural Verilog: 2 circuits, main circuit main
module main (
  input  [7:0] in_1,
  input  in_2
);

  wire clock_1_out, Control_alu, Control_memtoreg, Control_memwrite, Control_regdst, Control_regwrite;
  wire [1:0] Control_aluop, INSTRUCTION_MEMORY_PC_msb, INSTRUCTION_MEMORY_PC_out_9,
       INSTRUCTION_MEMORY_PC_out_11, INSTRUCTION_MEMORY_PC_out_13, multiplexer_1_out;
  wire [3:0] ALU_output, b_1_dataout, multiplexer_2_out, multiplexer_3_out, Registers_readdata1,
       Registers_readdata2;

  Q4B3_main INSTRUCTION_MEMORY_PC (
    .Reset(in_2), .CLK(clock_1_out), .Data_In(in_1), .RAM_Reset(1'b0), .MemWrite(1'b1),
    .Mem_Read_Write(1'b0), .MSB(INSTRUCTION_MEMORY_PC_msb[0]), .out_8(INSTRUCTION_MEMORY_PC_msb[1]),
    .out_9(INSTRUCTION_MEMORY_PC_out_9[0]), .out_10(INSTRUCTION_MEMORY_PC_out_9[1]),
    .out_11(INSTRUCTION_MEMORY_PC_out_11[0]), .out_12(INSTRUCTION_MEMORY_PC_out_11[1]),
    .out_13(INSTRUCTION_MEMORY_PC_out_13[0]), .LSB(INSTRUCTION_MEMORY_PC_out_13[1]));
  Clock clock_1 (.out(clock_1_out));
  Multiplexer #(.width(2), .enable("false")) multiplexer_1 (
    .in0(INSTRUCTION_MEMORY_PC_out_9), .in1(INSTRUCTION_MEMORY_PC_out_13), .out(multiplexer_1_out),
    .sel(Control_regdst));
  ControlTruth Control (
    .OpCode(INSTRUCTION_MEMORY_PC_msb), .RegDst(Control_regdst), .ALU(Control_alu),
    .MemtoReg(Control_memtoreg), .RegWrite(Control_regwrite), .MemWrite(Control_memwrite),
    .ALUOp(Control_aluop));  // open: MemRead
  reg_file Registers (
    .WriteData(multiplexer_2_out), .WriteReg(multiplexer_1_out), .RegWrite(Control_regwrite),
    .Clock(clock_1_out), .ReadData1(Registers_readdata1), .ReadReg1(INSTRUCTION_MEMORY_PC_out_9),
    .ReadData2(Registers_readdata2), .ReadReg2(INSTRUCTION_MEMORY_PC_out_11));
  Multiplexer #(.width(4), .enable("false")) multiplexer_2 (
    .in0(b_1_dataout), .in1(ALU_output), .out(multiplexer_2_out), .sel(Control_memtoreg));
  Multiplexer #(.width(4), .enable("false")) multiplexer_3 (
    .in0(Registers_readdata2), .in1({INSTRUCTION_MEMORY_PC_out_13, 2'b00}), .out(multiplexer_3_out),
    .sel(Control_alu));
  ALU ALU (
    .Input1(Registers_readdata1), .Input2(multiplexer_3_out), .ControlBits(Control_aluop), .Output(ALU_output));  // open: CarryOut, Zero
  b b_1 (
    .Address(ALU_output), .DataLoad(Registers_readdata1), .Store(Control_memwrite), .DataOut(b_1_dataout),
    .CLK(clock_1_out));  // open: Offset

  // Notes on the sheet:
  //   OP
  //   RS
  //   RT
  //   RD/Offset
endmodule

module main2 (
  input  [7:0] DataIn
);

  wire Control_alu, Control_memtoreg, Control_memwrite, Control_regdst, Control_regwrite, not_1_out;
  wire [1:0] Control_aluop, main_1_p3, main_1_p5, main_1_p7, main_1_p9, multiplexer_1_out, multiplexer_2_out;
  wire [3:0] ALU_output, b_1_dataout, multiplexer_3_out, multiplexer_4_out, RegFile_readdata1,
       RegFile_readdata2;

  // Q4B3_main main_1: pin names not known; wires that end beside it: DataIn, 1'b1, main_1_p3[0], main_1_p3[1], main_1_p5[0], main_1_p5[1], main_1_p7[0], main_1_p7[1], main_1_p9[0], main_1_p9[1]
  Multiplexer #(.width(2), .enable("false")) multiplexer_1 (
    .in0(main_1_p7), .in1(main_1_p9), .out(multiplexer_1_out), .sel(not_1_out));
  not not_1 (not_1_out, Control_regdst);
  Multiplexer #(.width(2), .enable("false")) multiplexer_2 (
    .in0(main_1_p7), .in1(main_1_p9), .out(multiplexer_2_out), .sel(Control_regdst));
  Multiplexer #(.width(4), .enable("false")) multiplexer_3 (
    .in0(ALU_output), .in1(b_1_dataout), .out(multiplexer_3_out), .sel(Control_memtoreg));
  reg_file RegFile (
    .WriteData(multiplexer_3_out), .WriteReg(multiplexer_1_out), .RegWrite(Control_regwrite),
    .ReadData1(RegFile_readdata1), .ReadReg1(main_1_p5), .ReadData2(RegFile_readdata2),
    .ReadReg2(multiplexer_2_out));  // open: Clock
  ControlTruth Control (
    .OpCode(main_1_p3), .RegDst(Control_regdst), .ALU(Control_alu), .MemtoReg(Control_memtoreg),
    .RegWrite(Control_regwrite), .MemWrite(Control_memwrite), .ALUOp(Control_aluop));  // open: MemRead
  ALU ALU (
    .Input1(RegFile_readdata1), .Input2(multiplexer_4_out), .ControlBits(Control_aluop), .Output(ALU_output));  // open: CarryOut, Zero
  Multiplexer #(.width(4), .enable("false")) multiplexer_4 (
    .in0(RegFile_readdata2), .in1({main_1_p9, 2'b00}), .out(multiplexer_4_out), .sel(Control_alu));
  b b_1 (
    .Address(ALU_output), .DataLoad(RegFile_readdata2), .Store(Control_memwrite), .DataOut(b_1_dataout));  // open: Offset, CLK

  // Notes on the sheet:
  //   OP
  //   RS
  //   RT
  //   RD/Offset
endmodule
